# Fritzing sketch AD8403_VCF (saved by Fritzing 0.9.2b)
breadboards: 2

parts:
  U1 = mystery part, 24 pins [chip_label=AD8403]
  パーツ1 = Arduino Uno (Rev3)
  C1 = Ceramic Capacitor [capacitance=100nF package="100 mil [THT, multilayer]"]
  IC1 = Dual Op-Amp [package=dip08]
  C2 = Ceramic Capacitor [capacitance=100nF package="100 mil [THT, multilayer]"]
  R1 = Resistor [tolerance=±5% resistance=10k package=THT]
  C3 = Ceramic Capacitor [capacitance=100nF package="100 mil [THT, multilayer]"]
  R2 = Resistor [tolerance=±5% resistance=10k package=THT]
  C4 = Ceramic Capacitor [capacitance=100nF package="100 mil [THT, multilayer]"]
  C5 = Ceramic Capacitor [capacitance=100nF package="100 mil [THT, multilayer]"]

nets:
  N1: U1.pin9, U1.pin21, U1.pin24, パーツ1.GND, C1.0, IC1.A_V-, IC1.B_+IN, C2.1, C4.0, C5.0
  N2: U1.pin10, U1.pin15, U1.pin16, パーツ1.5V, C1.1
  N3: U1.pin11, パーツ1.D10_PWM/SS
  N4: U1.pin12, パーツ1.D11_PWM/MOSI
  N5: U1.pin14, パーツ1.D13/SCK
  N6: U1.pin22, IC1.A_-IN
  N7: U1.pin23, IC1.A_OUT, C3.0
  N8: IC1.A_+IN, C2.0, R1.Pin_1
  N9: IC1.B_-IN, IC1.B_OUT
  N10: IC1.A_V+, C4.1
  N11: R1.Pin_0, C3.1, R2.Pin_1

notes:
  AD8403
  1:AGND2 24:B1
  2:B2 23:A1
  3:A2 22:W1
  4:W2 21:AGND1
  5:AGND4 20:B3
  6:B4 19:A3
  7:A4 18:W3
  8:W4 17:AGND3
  9:DGND 16:VDD
  10:!SHDN 15:!RS
  11:!CS 14:CLK
  12:SDI 13:SDO
  WAVE IN
  GND
  +5V
  -5V
  GND
