# Fritzing sketch AD8403_VCF_Cutoff_Q_Control (saved by Fritzing 0.9.2b)
breadboards: 2

parts:
  U1 = mystery part, 24 pins [chip_label=AD8403]
  パーツ1 = Arduino Uno (Rev3)
  C1 = Ceramic Capacitor [capacitance=100nF package="100 mil [THT, multilayer]"]
  IC1 = Dual Op-Amp [package=dip08]
  C2 = Ceramic Capacitor [capacitance=100nF package="100 mil [THT, multilayer]"]
  C3 = Ceramic Capacitor [capacitance=100nF package="100 mil [THT, multilayer]"]
  C4 = Ceramic Capacitor [capacitance=100nF package="100 mil [THT, multilayer]"]
  C5 = Ceramic Capacitor [capacitance=100nF package="100 mil [THT, multilayer]"]
  R1 = Rotary Potentiometer (Small) [maximum_resistance=100kΩ package=THT]
  R2 = Rotary Potentiometer (Small) [maximum_resistance=100kΩ package=THT]
  VCC1 = 4 x AAA Battery Mount
  VCC2 = 4 x AAA Battery Mount
  R3 = Rotary Potentiometer (Small) [maximum_resistance=100kΩ package=THT]

nets:
  N1: U1.pin1, U1.pin5, U1.pin9, U1.pin17, U1.pin21, U1.pin24, パーツ1.GND, C1.0, IC1.B_+IN, C4.0, C5.1, R1.leg1, R2.leg1, VCC1.-, VCC2.+, R3.leg1
  N2: U1.pin3, U1.pin4, U1.pin6, C3.1
  N3: U1.pin7, U1.pin8, IC1.A_+IN, C2.0
  N4: U1.pin10, U1.pin15, U1.pin16, パーツ1.5V, C1.1, R1.leg2, R2.leg2, R3.leg2
  N5: U1.pin11, パーツ1.D10_PWM/SS
  N6: U1.pin12, パーツ1.D11_PWM/MOSI
  N7: U1.pin14, パーツ1.D13/SCK
  N8: U1.pin22, IC1.A_-IN
  N9: U1.pin23, IC1.A_OUT, C3.0
  N10: パーツ1.A0, R2.wiper
  N11: パーツ1.A1, R1.wiper
  N12: パーツ1.A3, R3.wiper
  N13: IC1.A_V-, C2.1, C5.0, VCC2.-
  N14: IC1.B_-IN, IC1.B_OUT
  N15: IC1.A_V+, C4.1, VCC1.+

notes:
  AD8403
  1:AGND2 24:B1
  2:B2 23:A1
  3:A2 22:W1
  4:W2 21:AGND1
  5:AGND4 20:B3
  6:B4 19:A3
  7:A4 18:W3
  8:W4 17:AGND3
  9:DGND 16:VDD
  10:!SHDN 15:!RS
  11:!CS 14:CLK
  12:SDI 13:SDO
  WAVE IN
  GND
  +5V
  -5V
  GND
  Q
  Freq
  Option
