# Fritzing sketch DCF_AD8403_Shield_5VSupply (saved by Fritzing 0.9.2b)
breadboards: 2

parts:
  U1 = mystery part, 24 pins [chip_label=AD8403]
  IC1 = Dual Op-Amp [package=dip08]
  C2 = Ceramic Capacitor [capacitance=100nF package="100 mil [THT, multilayer]"]
  C3 = Ceramic Capacitor [capacitance=100nF package="100 mil [THT, multilayer]"]
  R1 = Resistor [tolerance=±5% resistance=100k package=THT]
  R2 = Resistor [tolerance=±5% resistance=100k package=THT]
  R3 = Resistor [tolerance=±5% resistance=1k package=THT]
  LED1 = LED - 5mm [color="Green (570nm)" package="5 mm [THT]"]
  C4 = Electrolytic Capacitor [capacitance=1µF package="100 mil [THT, electrolytic]"]
  C5 = Electrolytic Capacitor [capacitance=1µF package="100 mil [THT, electrolytic]"]
  パーツ1 = Arduino Uno (Rev3)
  JP1 = RCA [package=rca_lock]
  JP2 = RCA [package=rca_lock]
  C6 = Ceramic Capacitor [capacitance=100nF package="100 mil [THT, multilayer]"]
  R4 = Resistor [tolerance=±5% resistance=10k package=THT]
  C7 = Electrolytic Capacitor [capacitance=1µF package="100 mil [THT, electrolytic]"]
  C8 = Ceramic Capacitor [capacitance=100nF package="100 mil [THT, multilayer]"]
  C9 = Ceramic Capacitor [capacitance=100nF package="100 mil [THT, multilayer]"]

nets:
  N1: U1.pin1, U1.pin5, U1.pin9, U1.pin17, U1.pin20, U1.pin24, IC1.A_V-, R2.Pin_1, LED1.cathode, C5.-, パーツ1.GND, C6.1, C8.0
  N2: U1.pin2, IC1.A_+IN, C3.0
  N3: U1.pin3, U1.pin4, U1.pin6, C2.0
  N4: U1.pin7, U1.pin8, JP1.PIN
  N5: U1.pin10, U1.pin15, U1.pin16, IC1.A_V+, R1.Pin_0, R3.Pin_0, C4.+, パーツ1.5V, C6.0, C9.1
  N6: U1.pin11, パーツ1.D10_PWM/SS
  N7: U1.pin12, パーツ1.D11_PWM/MOSI
  N8: U1.pin14, パーツ1.D13/SCK
  N9: U1.pin21, IC1.B_-IN, IC1.B_OUT, C3.1, C4.-, C5.+, JP1.SHELL, JP2.SHELL, R4.Pin_0, C8.1, C9.0
  N10: U1.pin22, IC1.A_-IN
  N11: U1.pin23, IC1.A_OUT, C2.1, R4.Pin_1, C7.-
  N12: IC1.B_+IN, R1.Pin_1, R2.Pin_0
  N13: R3.Pin_1, LED1.anode
  N14: JP2.PIN, C7.+

notes:
  GND
  VDD/2
  VDD/2
  VDD
  GND
  VDD
  IN
  OUT
